// Logisim project 2MOD5.circ as structural Verilog: 2 circuits, main circuit mod5
module \状态转移  (
  input  I1,
  input  [1:0] IN,
  output [1:0] OUT
);

  wire nand_1_out, nand_2_out, nand_3_out, nand_4_out, nand_5_out, nand_6_out, nand_7_out, nand_8_out,
       nand_9_out, nand_10_out, nand_11_out, nand_12_out, nand_14_out, nand_15_out, nand_16_out, nand_17_out,
       nand_18_out, nand_19_out, nand_20_out, nand_21_out, nand_22_out, nand_23_out, nand_24_out,
       nand_25_out, nand_26_out, nand_27_out;

  nand nand_1 (nand_1_out, IN[1], IN[1]);
  nand nand_2 (nand_2_out, IN[0], IN[0]);
  nand nand_3 (nand_3_out, IN[1], IN[1]);
  nand nand_4 (nand_4_out, IN[0], IN[0]);
  nand nand_5 (nand_5_out, IN[1], IN[1]);
  nand nand_6 (nand_6_out, IN[0], IN[0]);
  nand nand_7 (nand_7_out, nand_1_out, IN[0]);
  nand nand_8 (nand_8_out, IN[1], nand_2_out);
  nand nand_9 (nand_9_out, nand_3_out, nand_4_out);
  nand nand_10 (nand_10_out, nand_5_out, IN[0]);
  nand nand_11 (nand_11_out, IN[1], nand_6_out);
  nand nand_12 (nand_12_out, IN[1], IN[0]);
  nand nand_13 (OUT[1], nand_7_out, nand_8_out);
  nand nand_14 (nand_14_out, nand_9_out, nand_9_out);
  nand nand_15 (nand_15_out, nand_10_out, nand_10_out);
  nand nand_16 (nand_16_out, I1, I1);
  nand nand_17 (nand_17_out, nand_11_out, nand_11_out);
  nand nand_18 (nand_18_out, I1, I1);
  nand nand_19 (nand_19_out, nand_12_out, nand_12_out);
  nand nand_20 (nand_20_out, nand_14_out, I1);
  nand nand_21 (nand_21_out, nand_15_out, nand_16_out);
  nand nand_22 (nand_22_out, nand_17_out, nand_18_out);
  nand nand_23 (nand_23_out, nand_19_out, I1);
  nand nand_24 (nand_24_out, nand_20_out, nand_21_out);
  nand nand_25 (nand_25_out, nand_22_out, nand_23_out);
  nand nand_26 (nand_26_out, nand_24_out, nand_24_out);
  nand nand_27 (nand_27_out, nand_25_out, nand_25_out);
  nand nand_28 (OUT[0], nand_26_out, nand_27_out);
endmodule

module mod5 (
  input  in_1,
  output S0,
  output S1,
  output S2,
  output S3,
  output S4
);

  wire clock_1_out;
  wire [1:0] register_1_q, \状态转移_1_out ;

  \状态转移  \u_状态转移_1  (.I1(in_1), .IN(register_1_q), .OUT(\状态转移_1_out ));
  Register #(.width(2)) register_1 (.D(\状态转移_1_out ), .Q(register_1_q), .clk(clock_1_out));  // open: en, clr
  Clock clock_1 (.out(clock_1_out));
  Decoder #(.select(2), .enable("false")) decoder_1 (.out0(S1), .out1(S2), .out2(S3), .out3(S4), .sel(\状态转移_1_out ));

  assign S0 = 1'b0;
endmodule
