// Logisim project CRC.circ as structural Verilog: 4 circuits, main circuit main
module main (
  input  [7:0] A,
  input  [3:0] B,
  output [10:0] C
);

  wire [2:0] mod_2_out_3, mod_3_out_3, mod_4_out_3, mod_5_out_3, mod_6_out_3, mod_7_out_3, mod_out_3;
  wire [3:0] ge_2_out_3, ge_3_out_3, ge_4_out_3, ge_out_3, generate_1_out_3, generate_2_out_3,
       generate_3_out_3;

  mod mod (.in_1(A[7:4]), .in_2(B), .out_3(mod_out_3));
  // Probe on mod_out_3
  \generate  ge (.in_1(A[3]), .in_2(mod_out_3), .out_3(ge_out_3));
  \generate  ge_2 (.in_1(A[2]), .in_2(mod_2_out_3), .out_3(ge_2_out_3));
  mod mod_2 (.in_1(ge_out_3), .in_2(B), .out_3(mod_2_out_3));
  // Probe on mod_2_out_3
  mod mod_3 (.in_1(ge_2_out_3), .in_2(B), .out_3(mod_3_out_3));
  // Probe on mod_3_out_3
  \generate  ge_3 (.in_1(A[1]), .in_2(mod_3_out_3), .out_3(ge_3_out_3));
  mod mod_4 (.in_1(ge_3_out_3), .in_2(B), .out_3(mod_4_out_3));
  // Probe on mod_4_out_3
  \generate  ge_4 (.in_1(A[0]), .in_2(mod_4_out_3), .out_3(ge_4_out_3));
  \generate  generate_1 (.in_1(1'b0), .in_2(mod_5_out_3), .out_3(generate_1_out_3));
  mod mod_5 (.in_1(ge_4_out_3), .in_2(B), .out_3(mod_5_out_3));
  // Probe on mod_5_out_3
  mod mod_6 (.in_1(generate_1_out_3), .in_2(B), .out_3(mod_6_out_3));
  mod mod_7 (.in_1(generate_2_out_3), .in_2(B), .out_3(mod_7_out_3));
  \generate  generate_2 (.in_1(1'b0), .in_2(mod_6_out_3), .out_3(generate_2_out_3));
  \generate  generate_3 (.in_1(1'b0), .in_2(mod_7_out_3), .out_3(generate_3_out_3));
  mod mod_8 (.in_1(generate_3_out_3), .in_2(B), .out_3(C[2:0]));

  assign C[10:3] = A;

  // Other names for the same wires on the sheet: check[2:0] = C[2:0]
endmodule

module mod (
  input  [3:0] in_1,
  input  [3:0] in_2,
  output [2:0] out_3
);

  wire comparator_1_eq;
  wire [1:0] bitfinder_1_index;
  wire [2:0] _1;
  wire [3:0] shifter_1_out;

  BitFinder #(.width(4), .\type ("high1")) bitfinder_1 (.in(in_1), .index(bitfinder_1_index));  // open: found
  Shifter #(.width(4)) shifter_1 (.in(4'b0001), .\dist (bitfinder_1_index), .out(shifter_1_out));
  Comparator #(.width(4)) comparator_1 (.a(shifter_1_out), .b(4'b1000), .eq(comparator_1_eq));  // open: gt, lt
  mod0 mod0_1 (.\_4位被除 (in_1), .\除数 (in_2), .\商 (_1));
  Multiplexer #(.width(3), .enable("false")) multiplexer_1 (
    .in0(in_1[2:0]), .in1(_1), .out(out_3), .sel(comparator_1_eq));

  // Other names for the same wires on the sheet: _2[2:0] = in_1[2:0]; 被除[3:0] = in_1; 除数[3:0] = in_2
endmodule

module mod0 (
  input  [3:0] \_4位被除 ,
  input  [3:0] \除数 ,
  output [2:0] \商 
);

  wire [3:3] xor_1_out;

  assign {xor_1_out[3], \商 } = \_4位被除  ^ \除数 ;  // XOR_Gate xor_1, 4 bits wide
  // Probe on {xor_1_out[3], \商 }
endmodule

module \generate  (
  input  in_1,
  input  [2:0] in_2,
  output [3:0] out_3
);


  assign out_3 = {in_2, in_1};
endmodule
