// Logisim project GRF.circ as structural Verilog: 1 circuit, main circuit main
module main (
  input  reset,
  input  clk,
  input  WE,
  input  [4:0] A1,
  input  [4:0] A2,
  input  [4:0] A3,
  input  [31:0] WD,
  output [31:0] RD1,
  output [31:0] RD2
);

  wire [31:0] i1, i2, i3, i4, i5, i6, i7, i8, i9, i10, i11, i12, i13, i14, i15, i16, i17, i18, i19, i20, i21,
       i22, i23, i24, i25, i26, i27, i28, i29, i30, i31, i32, o1, o2, o3, o4, o5, o6, o7, o8, o9, o10, o11,
       o12, o13, o14, o15, o16, o17, o18, o19, o20, o21, o22, o23, o24, o25, o26, o27, o28, o29, o30, o31,
       o32;

  Multiplexer #(.select(5), .width(32), .enable("false")) multiplexer_1 (
    .in0(o1), .in1(o2), .in2(o3), .in3(o4), .in4(o5), .in5(o6), .in6(o7), .in7(o8), .in8(o9), .in9(o10),
    .in10(o11), .in11(o12), .in12(o13), .in13(o14), .in14(o15), .in15(o16), .in16(o17), .in17(o18),
    .in18(o19), .in19(o20), .in20(o21), .in21(o22), .in22(o23), .in23(o24), .in24(o25), .in25(o26),
    .in26(o27), .in27(o28), .in28(o29), .in29(o30), .in30(o31), .in31(o32), .out(RD1), .sel(A1));
  Multiplexer #(.select(5), .width(32), .enable("false")) multiplexer_2 (
    .in0(o1), .in1(o2), .in2(o3), .in3(o4), .in4(o5), .in5(o6), .in6(o7), .in7(o8), .in8(o9), .in9(o10),
    .in10(o11), .in11(o12), .in12(o13), .in13(o14), .in14(o15), .in15(o16), .in16(o17), .in17(o18),
    .in18(o19), .in19(o20), .in20(o21), .in21(o22), .in22(o23), .in23(o24), .in24(o25), .in25(o26),
    .in26(o27), .in27(o28), .in28(o29), .in29(o30), .in30(o31), .in31(o32), .out(RD2), .sel(A2));
  Register #(.width(32)) register_1 (.D(i1), .en(WE), .Q(o1), .clk(clk), .clr(reset));
  Register #(.width(32)) register_2 (.D(i5), .en(WE), .Q(o5), .clk(clk), .clr(reset));
  Register #(.width(32)) register_3 (.D(i9), .en(WE), .Q(o9), .clk(clk), .clr(reset));
  Register #(.width(32)) register_4 (.D(i13), .en(WE), .Q(o13), .clk(clk), .clr(reset));
  Register #(.width(32)) register_5 (.D(i17), .en(WE), .Q(o17), .clk(clk), .clr(reset));
  Register #(.width(32)) register_6 (.D(i21), .en(WE), .Q(o21), .clk(clk), .clr(reset));
  Register #(.width(32)) register_7 (.D(i25), .en(WE), .Q(o25), .clk(clk), .clr(reset));
  Register #(.width(32)) register_8 (.D(i29), .en(WE), .Q(o29), .clk(clk), .clr(reset));
  Demultiplexer #(.select(5), .width(32), .enable("false")) demultiplexer_1 (
    .out0(i1), .out1(i2), .out2(i3), .out3(i4), .out4(i5), .out5(i6), .out6(i7), .out7(i8), .out8(i9),
    .out9(i10), .out10(i11), .out11(i12), .out12(i13), .out13(i14), .out14(i15), .out15(i16), .out16(i17),
    .out17(i18), .out18(i19), .out19(i20), .out20(i21), .out21(i22), .out22(i23), .out23(i24), .out24(i25),
    .out25(i26), .out26(i27), .out27(i28), .out28(i29), .out29(i30), .out30(i31), .out31(i32), .in(WD),
    .sel(A3));
  Register #(.width(32)) register_9 (.D(i2), .en(WE), .Q(o2), .clk(clk), .clr(reset));
  Register #(.width(32)) register_10 (.D(i6), .en(WE), .Q(o6), .clk(clk), .clr(reset));
  Register #(.width(32)) register_11 (.D(i10), .en(WE), .Q(o10), .clk(clk), .clr(reset));
  Register #(.width(32)) register_12 (.D(i14), .en(WE), .Q(o14), .clk(clk), .clr(reset));
  Register #(.width(32)) register_13 (.D(i18), .en(WE), .Q(o18), .clk(clk), .clr(reset));
  Register #(.width(32)) register_14 (.D(i22), .en(WE), .Q(o22), .clk(clk), .clr(reset));
  Register #(.width(32)) register_15 (.D(i26), .en(WE), .Q(o26), .clk(clk), .clr(reset));
  Register #(.width(32)) register_16 (.D(i30), .en(WE), .Q(o30), .clk(clk), .clr(reset));
  Register #(.width(32)) register_17 (.D(i3), .en(WE), .Q(o3), .clk(clk), .clr(reset));
  Register #(.width(32)) register_18 (.D(i7), .en(WE), .Q(o7), .clk(clk), .clr(reset));
  Register #(.width(32)) register_19 (.D(i11), .en(WE), .Q(o11), .clk(clk), .clr(reset));
  Register #(.width(32)) register_20 (.D(i15), .en(WE), .Q(o15), .clk(clk), .clr(reset));
  Register #(.width(32)) register_21 (.D(i19), .en(WE), .Q(o19), .clk(clk), .clr(reset));
  Register #(.width(32)) register_22 (.D(i23), .en(WE), .Q(o23), .clk(clk), .clr(reset));
  Register #(.width(32)) register_23 (.D(i27), .en(WE), .Q(o27), .clk(clk), .clr(reset));
  Register #(.width(32)) register_24 (.D(i31), .en(WE), .Q(o31), .clk(clk), .clr(reset));
  Register #(.width(32)) register_25 (.D(i4), .en(WE), .Q(o4), .clk(clk), .clr(reset));
  Register #(.width(32)) register_26 (.D(i8), .en(WE), .Q(o8), .clk(clk), .clr(reset));
  Register #(.width(32)) register_27 (.D(i12), .en(WE), .Q(o12), .clk(clk), .clr(reset));
  Register #(.width(32)) register_28 (.D(i16), .en(WE), .Q(o16), .clk(clk), .clr(reset));
  Register #(.width(32)) register_29 (.D(i20), .en(WE), .Q(o20), .clk(clk), .clr(reset));
  Register #(.width(32)) register_30 (.D(i24), .en(WE), .Q(o24), .clk(clk), .clr(reset));
  Register #(.width(32)) register_31 (.D(i28), .en(WE), .Q(o28), .clk(clk), .clr(reset));
  Register #(.width(32)) register_32 (.D(i32), .en(WE), .Q(o32), .clk(clk), .clr(reset));

  // Other names for the same wires on the sheet: enable = WE; in1[4:0] = A1; in2[4:0] = A2; in3[4:0] = A3;
  //   indata[31:0] = WD; out1[31:0] = RD1; out2[31:0] = RD2
endmodule
