// Logisim project challenge.circ as structural Verilog: 4 circuits, main circuit main
module main (
  input  [31:0] N,
  output [31:0] out_2
);

  wire clk, comparator_2_eq, counter_1_q, counter_2_q, counter_3_q, counter_4_q, en, equal;
  wire [31:0] and_1_out, calcu_1_o1, calcu_1_o2, calcu_1_o3, calcu_1_o4, multiplexer_1_out, o1, o3,
       realcalcu_1_o1, realcalcu_1_o2, realcalcu_1_o3, realcalcu_1_o4, realcalcu_2_o1, realcalcu_2_o2,
       realcalcu_2_o3, realcalcu_2_o4, register_1_q, shifter_1_out, store_1_o1, store_1_o2, store_1_o3,
       store_1_o4;

  Multiplexer #(.width(32), .enable("false")) multiplexer_1 (
    .in0(N), .in1(shifter_1_out), .out(multiplexer_1_out), .sel(counter_1_q));
  Counter #(.width(1), .max('h1), .ongoal("stay")) counter_1 (
    .Q(counter_1_q), .clk(clk), .clr(1'b0));  // open: load, D, count, carry
  Clock clock_1 (.out(clk));
  Register #(.width(32)) register_1 (.D(multiplexer_1_out), .Q(register_1_q), .clk(clk), .clr(1'b0));  // open: en
  realcalcu realcalcu_1 (
    .o1(realcalcu_1_o1), .o3(realcalcu_1_o3), .o2(realcalcu_1_o2), .o4(realcalcu_1_o4), .in11(calcu_1_o1),
    .in12(calcu_1_o2), .in13(calcu_1_o3), .in14(calcu_1_o4), .in21(calcu_1_o1), .in22(calcu_1_o2),
    .in23(calcu_1_o3), .in24(calcu_1_o4));
  Shifter #(.width(32), .shift("lr")) shifter_1 (.in(register_1_q), .\dist (5'b00001), .out(shifter_1_out));
  assign and_1_out = register_1_q & 32'h1;  // AND_Gate and_1, 32 bits wide
  calcu calcu_1 (
    .clk(clk), .i2(realcalcu_1_o2), .in_3(1'b0), .i1(realcalcu_1_o1), .i3(realcalcu_1_o3),
    .i4(realcalcu_1_o4), .o1(calcu_1_o1), .o2(calcu_1_o2), .o3(calcu_1_o3), .o4(calcu_1_o4));
  Comparator #(.width(32), .mode("unsigned")) comparator_1 (.a(and_1_out), .b(32'h1), .eq(equal));  // open: gt, lt
  realcalcu realcalcu_2 (
    .o1(realcalcu_2_o1), .o3(realcalcu_2_o3), .o2(realcalcu_2_o2), .o4(realcalcu_2_o4), .in11(store_1_o1),
    .in12(store_1_o2), .in13(store_1_o4), .in14(store_1_o3), .in21(calcu_1_o1), .in22(calcu_1_o2),
    .in23(calcu_1_o3), .in24(calcu_1_o4));
  Comparator #(.width(32), .mode("unsigned")) comparator_2 (
    .a(register_1_q), .b({32{1'b0}}), .eq(comparator_2_eq));  // open: gt, lt
  store store_1 (
    .clk(clk), .en(en), .reset(1'b0), .i2(realcalcu_2_o2), .i1(o1), .i3(o3), .i4(realcalcu_2_o4),
    .o1(store_1_o1), .o2(store_1_o2), .o4(store_1_o4), .o3(store_1_o3));
  Counter #(.width(1), .max('h1), .ongoal("stay")) counter_2 (
    .Q(counter_2_q), .clk(clk), .clr(1'b0));  // open: load, D, count, carry
  Multiplexer #(.width(32), .enable("false")) multiplexer_2 (
    .in0(32'h1), .in1(realcalcu_2_o1), .out(o1), .sel(counter_3_q));
  Counter #(.width(1), .max('h1), .ongoal("stay")) counter_3 (
    .Q(counter_3_q), .clk(clk), .clr(1'b0));  // open: load, D, count, carry
  Multiplexer #(.width(32), .enable("false")) multiplexer_3 (
    .in0(32'h1), .in1(realcalcu_2_o3), .out(o3), .sel(counter_2_q));
  Multiplexer #(.enable("false")) multiplexer_4 (.in0(1'b1), .in1(equal), .out(en), .sel(counter_4_q));
  Counter #(.width(1), .max('h1), .ongoal("stay")) counter_4 (
    .Q(counter_4_q), .clk(clk), .clr(1'b0));  // open: load, D, count, carry
  Multiplexer #(.width(32), .enable("false")) multiplexer_5 (
    .in0({32{1'b0}}), .in1(store_1_o2), .out(out_2), .sel(comparator_2_eq));
endmodule

module store (
  input  clk,
  input  en,
  input  reset,
  input  [31:0] i1,
  input  [31:0] i2,
  input  [31:0] i3,
  input  [31:0] i4,
  output [31:0] o1,
  output [31:0] o2,
  output [31:0] o4,
  output [31:0] o3
);

  Register #(.width(32)) register_1 (.D(i1), .en(en), .Q(o1), .clk(clk), .clr(reset));
  Register #(.width(32)) register_2 (.D(i3), .en(en), .Q(o3), .clk(clk), .clr(reset));
  Register #(.width(32)) register_3 (.D(i2), .en(en), .Q(o2), .clk(clk), .clr(reset));
  Register #(.width(32)) register_4 (.D(i4), .en(en), .Q(o4), .clk(clk), .clr(reset));
endmodule

module calcu (
  input  clk,
  input  [31:0] i2,
  input  in_3,
  input  [31:0] i1,
  input  [31:0] i3,
  input  [31:0] i4,
  output [31:0] o1,
  output [31:0] o2,
  output [31:0] o3,
  output [31:0] o4
);

  wire counter_1_q, counter_2_q, counter_3_q, counter_4_q;
  wire [31:0] multiplexer_1_out, multiplexer_2_out, multiplexer_3_out, multiplexer_4_out;

  Counter #(.width(1), .max('h1), .ongoal("stay")) counter_1 (
    .Q(counter_1_q), .clk(clk), .clr(in_3));  // open: load, D, count, carry
  Counter #(.width(1), .max('h1), .ongoal("stay")) counter_2 (
    .Q(counter_2_q), .clk(clk), .clr(in_3));  // open: load, D, count, carry
  Multiplexer #(.width(32), .enable("false")) multiplexer_1 (
    .in0(32'h1), .in1(i1), .out(multiplexer_1_out), .sel(counter_1_q));
  Multiplexer #(.width(32), .enable("false")) multiplexer_2 (
    .in0(32'h1), .in1(i3), .out(multiplexer_2_out), .sel(counter_2_q));
  Register #(.width(32)) register_1 (.D(multiplexer_1_out), .Q(o1), .clk(clk), .clr(in_3));  // open: en
  Register #(.width(32)) register_2 (.D(multiplexer_2_out), .Q(o3), .clk(clk), .clr(in_3));  // open: en
  Multiplexer #(.width(32), .enable("false")) multiplexer_3 (
    .in0(32'h1), .in1(i2), .out(multiplexer_3_out), .sel(counter_3_q));
  Counter #(.width(1), .max('h1), .ongoal("stay")) counter_3 (
    .Q(counter_3_q), .clk(clk), .clr(in_3));  // open: load, D, count, carry
  Multiplexer #(.width(32), .enable("false")) multiplexer_4 (
    .in0({32{1'b0}}), .in1(i4), .out(multiplexer_4_out), .sel(counter_4_q));
  Counter #(.width(1), .max('h1), .ongoal("stay")) counter_4 (
    .Q(counter_4_q), .clk(clk), .clr(in_3));  // open: load, D, count, carry
  Register #(.width(32)) register_3 (.D(multiplexer_3_out), .Q(o2), .clk(clk), .clr(in_3));  // open: en
  Register #(.width(32)) register_4 (.D(multiplexer_4_out), .Q(o4), .clk(clk), .clr(in_3));  // open: en

  // Other names for the same wires on the sheet: reset = in_3
endmodule

module realcalcu (
  input  [31:0] in11,
  input  [31:0] in12,
  input  [31:0] in13,
  input  [31:0] in14,
  input  [31:0] in21,
  input  [31:0] in22,
  input  [31:0] in23,
  input  [31:0] in24,
  output [31:0] o1,
  output [31:0] o3,
  output [31:0] o2,
  output [31:0] o4
);

  wire [31:0] multiplier_1_out, multiplier_2_out, multiplier_3_out, multiplier_4_out, multiplier_5_out,
       multiplier_6_out, multiplier_7_out, multiplier_8_out;

  Multiplier #(.width(32)) multiplier_1 (.a(in11), .b(in21), .out(multiplier_1_out));  // open: cin, cout
  Multiplier #(.width(32)) multiplier_2 (.a(in12), .b(in23), .out(multiplier_2_out));  // open: cin, cout
  Multiplier #(.width(32)) multiplier_3 (.a(in11), .b(in22), .out(multiplier_3_out));  // open: cin, cout
  Multiplier #(.width(32)) multiplier_4 (.a(in12), .b(in24), .out(multiplier_4_out));  // open: cin, cout
  Adder #(.width(32)) adder_1 (.a(multiplier_1_out), .b(multiplier_2_out), .out(o1));  // open: cin, cout
  Adder #(.width(32)) adder_2 (.a(multiplier_3_out), .b(multiplier_4_out), .out(o2));  // open: cin, cout
  Multiplier #(.width(32)) multiplier_5 (.a(in13), .b(in21), .out(multiplier_5_out));  // open: cin, cout
  Multiplier #(.width(32)) multiplier_6 (.a(in14), .b(in23), .out(multiplier_6_out));  // open: cin, cout
  Multiplier #(.width(32)) multiplier_7 (.a(in13), .b(in22), .out(multiplier_7_out));  // open: cin, cout
  Multiplier #(.width(32)) multiplier_8 (.a(in14), .b(in24), .out(multiplier_8_out));  // open: cin, cout
  Adder #(.width(32)) adder_3 (.a(multiplier_5_out), .b(multiplier_6_out), .out(o3));  // open: cin, cout
  Adder #(.width(32)) adder_4 (.a(multiplier_7_out), .b(multiplier_8_out), .out(o4));  // open: cin, cout

  // Other names for the same wires on the sheet: a1[31:0] = in11; a2[31:0] = in12; a3[31:0] = in13; a4[31:0] = in14;
  //   b1[31:0] = in21; b2[31:0] = in22; b3[31:0] = in23; b4[31:0] = in24
endmodule
