// Logisim project swap+排序.circ as structural Verilog: 3 circuits, main circuit 4bit_sort
module main (
  input  l1,
  input  S,
  input  l2,
  output O1,
  output O2
);

  wire and_1_out, and_2_out, and_3_out, and_4_out, and_5_out, and_6_out, and_7_out, and_8_out;

  and and_1 (and_1_out, l1, S, l2);
  and and_2 (and_2_out, ~l1, S, l2);  // AND_Gate
  and and_3 (and_3_out, l1, ~S, ~l2);  // AND_Gate
  and and_4 (and_4_out, l1, ~S, l2);  // AND_Gate
  and and_5 (and_5_out, l1, S, ~l2);  // AND_Gate
  and and_6 (and_6_out, l1, S, l2);
  and and_7 (and_7_out, l1, ~S, l2);  // AND_Gate
  and and_8 (and_8_out, ~l1, ~S, l2);  // AND_Gate
  or or_1 (O1, and_1_out, and_2_out, and_3_out, and_4_out);
  or or_2 (O2, and_5_out, and_6_out, and_7_out, and_8_out);
endmodule

module swap4 (
  input  S,
  input  [3:0] I1,
  input  [3:0] I2,
  output [3:0] O1,
  output [3:0] O2
);

  main main_1 (.S(S), .l2(I2[0]), .O1(O1[0]), .O2(O2[0]), .l1(I1[0]));
  main main_2 (.S(S), .l2(I2[1]), .O1(O1[1]), .O2(O2[1]), .l1(I1[1]));
  main main_3 (.S(S), .l2(I2[2]), .O1(O1[2]), .O2(O2[2]), .l1(I1[2]));
  main main_4 (.S(S), .l2(I2[3]), .O1(O1[3]), .O2(O2[3]), .l1(I1[3]));
endmodule

module _4bit_sort (
  input  [3:0] I1,
  input  [3:0] I3,
  input  [3:0] I2,
  input  [3:0] I4,
  output [3:0] O2,
  output [3:0] O3,
  output [3:0] O1,
  output [3:0] O4
);

  wire comparator_1_gt, comparator_2_gt, comparator_3_gt, comparator_4_gt, comparator_5_gt, comparator_6_gt;
  wire [3:0] max1, max2, max3, max10, max20, min1, min2, min10;

  swap4 swap4_1 (.S(comparator_1_gt), .I1(I1), .I2(I2), .O1(min1), .O2(max1));
  Comparator #(.width(4), .mode("unsigned")) comparator_1 (.a(I1), .b(I2), .gt(comparator_1_gt));  // open: eq, lt
  Comparator #(.width(4), .mode("unsigned")) comparator_2 (.a(I4), .b(min2), .gt(comparator_2_gt));  // open: eq, lt
  swap4 swap4_2 (.S(comparator_2_gt), .I1(I4), .I2(min2), .O1(O1), .O2(max3));
  Comparator #(.width(4), .mode("unsigned")) comparator_3 (.a(I3), .b(min1), .gt(comparator_3_gt));  // open: eq, lt
  swap4 swap4_3 (.S(comparator_3_gt), .I1(I3), .I2(min1), .O1(min2), .O2(max2));
  swap4 swap4_4 (.S(comparator_4_gt), .I1(max1), .I2(max2), .O1(min10), .O2(max20));
  Comparator #(.width(4), .mode("unsigned")) comparator_4 (.a(max1), .b(max2), .gt(comparator_4_gt));  // open: eq, lt
  Comparator #(.width(4), .mode("unsigned")) comparator_5 (.a(min10), .b(max3), .gt(comparator_5_gt));  // open: eq, lt
  swap4 swap4_5 (.S(comparator_5_gt), .I1(min10), .I2(max3), .O1(O2), .O2(max10));
  Comparator #(.width(4), .mode("unsigned")) comparator_6 (.a(max10), .b(max20), .gt(comparator_6_gt));  // open: eq, lt
  swap4 swap4_6 (.S(comparator_6_gt), .I1(max10), .I2(max20), .O1(O3), .O2(O4));
endmodule
