// Logisim project 斐波那契.circ as structural Verilog: 2 circuits, main circuit main
module \计数逻辑  (
  input  [2:0] in_1,
  output out_2
);

  wire clk, comparator_1_eq, comparator_1_gt;
  wire [3:0] bit_extender_1_out, counter_1_q;

  Clock clock_1 (.out(clk));
  Counter #(.width(4), .max('hf), .ongoal("stay")) counter_1 (
    .Q(counter_1_q), .clk(clk), .clr(1'b0));  // open: load, D, count, carry
  assign bit_extender_1_out = {{1{1'b0}}, in_1};  // Bit_Extender bit_extender_1
  // Probe on counter_1_q
  Comparator #(.width(4), .mode("unsigned")) comparator_1 (
    .a(counter_1_q), .b(bit_extender_1_out), .gt(comparator_1_gt), .eq(comparator_1_eq));  // open: lt
  nor nor_1 (out_2, comparator_1_gt, comparator_1_eq);
endmodule

module main (
  input  [2:0] in_1,
  output [3:0] out_2
);

  wire clk, counter_1_q, stop;
  wire [3:0] adder_1_out, multiplexer_1_out, now, prev;

  \计数逻辑  \u_计数逻辑_1  (.in_1(in_1), .out_2(stop));
  Multiplexer #(.width(4), .enable("false")) multiplexer_1 (
    .in0(4'b0001), .in1(now), .out(multiplexer_1_out), .sel(counter_1_q));
  Counter #(.width(1), .max('h1), .ongoal("stay")) counter_1 (
    .Q(counter_1_q), .clk(clk));  // open: load, D, count, carry, clr
  Clock clock_1 (.out(clk));
  Adder #(.width(4)) adder_1 (.a(prev), .b(multiplexer_1_out), .out(adder_1_out));  // open: cin, cout
  Multiplexer #(.width(4), .enable("false")) multiplexer_2 (.in0(now), .in1(4'b0000), .out(out_2), .sel(stop));
  Register #(.width(4)) register_1 (.D(now), .en(stop), .Q(prev), .clk(clk));  // open: clr
  Register #(.width(4)) register_2 (.D(adder_1_out), .en(stop), .Q(now), .clk(clk));  // open: clr
endmodule
