// Logisim project 正则匹配.circ as structural Verilog: 2 circuits, main circuit main
module main (
  input  [1:0] In,
  input  clk,
  input  clr,
  output Z
);

  wire [1:0] multiplexer_1_out, multiplexer_2_out, register_1_q, register_2_q, state;

  Multiplexer #(.width(2), .enable("false")) multiplexer_1 (
    .in0(state), .in1(2'b00), .out(multiplexer_1_out), .sel(clr));
  Register #(.width(2)) register_1 (.D(multiplexer_1_out), .Q(register_1_q), .clk(clk));  // open: en, clr
  Multiplexer #(.width(2), .enable("false")) multiplexer_2 (
    .in0(state), .in1(2'b00), .out(multiplexer_2_out), .sel(clr));
  trans trans_1 (.now(register_1_q), .step(In), .out_3(state));  // open: check
  Register #(.width(2)) register_2 (.D(multiplexer_2_out), .Q(register_2_q), .clk(clk), .clr(clr));  // open: en
  trans trans_2 (.now(register_2_q), .step(In), .check(Z));  // open: out_3

  // Other names for the same wires on the sheet: out = Z
endmodule

module trans (
  input  [1:0] now,
  input  [1:0] step,
  output [1:0] out_3,
  output check
);

  wire and_1_out, and_2_out, and_3_out, and_4_out, not_1_out, not_2_out, not_3_out, not_4_out, not_5_out,
       not_6_out, not_7_out, not_8_out, not_9_out;

  not not_1 (not_1_out, now[1]);
  not not_2 (not_2_out, step[0]);
  not not_3 (not_3_out, now[0]);
  not not_4 (not_4_out, step[0]);
  not not_5 (not_5_out, step[1]);
  not not_6 (not_6_out, now[0]);
  not not_7 (not_7_out, step[0]);
  not not_8 (not_8_out, now[0]);
  not not_9 (not_9_out, step[0]);
  and and_1 (and_1_out, not_1_out, now[0], not_2_out);
  or or_1 (out_3[1], and_1_out, and_2_out);
  and and_2 (and_2_out, now[1], not_3_out, not_4_out);
  and and_3 (and_3_out, not_5_out, step[0]);
  or or_2 (out_3[0], and_3_out, and_4_out);
  and and_4 (and_4_out, now[1], not_6_out, not_7_out);
  and and_5 (check, now[1], not_8_out, not_9_out);
endmodule
